// Logisim project Project.circ as structural Verilog: 3 circuits, main circuit main
module ALU (
  input  [15:0] DR,
  input  [15:0] AC,
  input  [2:0] in_3,
  output C_out_add,
  output C_out_sub,
  output [15:0] \output ,
  output out_7
);

  wire [15:0] adder_1_out, adder_2_out, and_1_out, or_1_out, subtractor_1_out, xor_1_out;

  assign and_1_out = DR & AC;  // AND_Gate and_1, 16 bits wide
  assign or_1_out = DR | AC;  // OR_Gate or_1, 16 bits wide
  assign xor_1_out = DR ^ AC;  // XOR_Gate xor_1, 16 bits wide
  Adder #(.width(16)) adder_1 (.a(DR), .b({16{1'b0}}), .out(adder_1_out), .cin(1'b1), .cout(out_7));
  Subtractor #(.width(16)) subtractor_1 (.a(DR), .b(AC), .out(subtractor_1_out), .bin(1'b0), .bout(C_out_sub));
  Adder #(.width(16)) adder_2 (.a(DR), .b(AC), .out(adder_2_out), .cin(1'b0), .cout(C_out_add));
  Multiplexer #(.select(3), .width(16), .enable("false")) multiplexer_1 (
    .in1(adder_2_out), .in2(subtractor_1_out), .in3(DR), .in4(and_1_out), .in5(or_1_out), .in6(xor_1_out),
    .in7(adder_1_out), .out(\output ), .sel(in_3));  // open: in0
endmodule

module main (
  output out_1,
  output out_2,
  output out_3
);

  wire clock_1_out, control_unit_1_clear_sc, D_flip_q, INC_PC, LD_AR, LD_DR, LD_IR, LD_PC, LD_TR, LDA_AC,
       Load, str;
  wire [2:0] ALU, control_unit_1_bus;
  wire [3:0] count_q;
  wire [6:0] AR_q, bit_extender_1_out, bit_extender_2_out, PC_q;
  wire [15:0] AC_inp, ALU_output, bit_extender_3_out, bit_extender_4_out, bit_extender_5_out, DR_q, IR_q,
       multiplexer_1_out, ram_1_data, TR_q;

  ALU u_ALU (
    .AC(AC_inp), .in_3(ALU), .\output (ALU_output), .C_out_sub(out_1), .C_out_add(out_3), .DR(DR_q),
    .out_7(out_2));
  Bit_Extender #(.in_width(16), .out_width(7)) bit_extender_1 (.in(multiplexer_1_out), .out(bit_extender_1_out));
  Bit_Extender #(.in_width(16), .out_width(7)) bit_extender_2 (.in(multiplexer_1_out), .out(bit_extender_2_out));
  D_Flip_Flop D_flip (.clk(clock_1_out), .D(control_unit_1_clear_sc), .Q(D_flip_q));  // open: Qn, preset, en, reset
  RAM #(.addrWidth(7), .dataWidth(16), .bus("separate")) ram_1 (
    .addr(AR_q), .din(multiplexer_1_out), .data(ram_1_data), .str(str), .clk(clock_1_out), .ld(Load));  // open: sel, clr
  Register #(.width(7)) AR (.D(bit_extender_1_out), .en(LD_AR), .Q(AR_q), .clk(clock_1_out));  // open: clr
  Register #(.width(16)) TR (.D(multiplexer_1_out), .en(LD_TR), .Q(TR_q), .clk(clock_1_out));  // open: clr
  Register #(.width(16)) DR (.D(multiplexer_1_out), .en(LD_DR), .Q(DR_q), .clk(clock_1_out));  // open: clr
  Register #(.width(16)) AC (.D(ALU_output), .en(LDA_AC), .Q(AC_inp), .clk(clock_1_out));  // open: clr
  Counter #(.width(7), .max('h7f)) PC (
    .load(LD_PC), .D(bit_extender_2_out), .count(INC_PC), .Q(PC_q), .clk(clock_1_out));  // open: carry, clr
  Register #(.width(16)) IR (.D(multiplexer_1_out), .en(LD_IR), .Q(IR_q), .clk(clock_1_out));  // open: clr
  Counter #(.width(4), .max('hf)) count (
    .Q(count_q), .clk(clock_1_out), .clr(D_flip_q));  // open: load, D, count, carry
  assign bit_extender_3_out = {{9{1'b0}}, AR_q};  // Bit_Extender bit_extender_3
  assign bit_extender_4_out = {{9{1'b0}}, PC_q};  // Bit_Extender bit_extender_4
  assign bit_extender_5_out = {{4{1'b0}}, IR_q[11:0]};  // Bit_Extender bit_extender_5
  Multiplexer #(.select(3), .width(16), .enable("false")) multiplexer_1 (
    .in0(ram_1_data), .in1(bit_extender_3_out), .in2(TR_q), .in3(DR_q), .in4(AC_inp),
    .in5(bit_extender_4_out), .in6(bit_extender_5_out), .out(multiplexer_1_out), .sel(control_unit_1_bus));  // open: in7
  Clock clock_1 (.out(clock_1_out));
  Control_Unit control_unit_1 (
    .B2(IR_q[2]), .IR_input(IR_q[14:12]), .AC_inp(AC_inp), .bus(control_unit_1_bus), .PC_inp(count_q),
    .LDA_IR(LD_IR), .LDA_AR(LD_AR), .LDA_PC(LD_PC), .LD_TR(LD_TR), .INC_PC(INC_PC), .LDA_DR(LD_DR),
    .str(str), .load(Load), .clear_sc(control_unit_1_clear_sc), .LDA_AC(LDA_AC), .ALU(ALU));
endmodule

module Control_Unit (
  input  B2,
  input  [2:0] IR_input,
  input  [15:0] AC_inp,
  input  [3:0] PC_inp,
  output LDA_IR,
  output LDA_AR,
  output LDA_PC,
  output LD_TR,
  output INC_PC,
  output LDA_DR,
  output str,
  output load,
  output clear_sc,
  output LDA_AC,
  output [2:0] ALU,
  output [2:0] bus
);

  wire and_1_out, and_3_out, and_4_out, and_5_out, and_7_out, and_8_out, and_9_out, and_11_out, and_12_out,
       and_13_out, and_14_out, and_15_out, and_16_out, and_17_out, and_18_out, and_19_out, and_20_out,
       and_21_out, and_22_out, and_23_out, and_24_out, and_25_out, and_26_out, and_28_out, and_29_out,
       and_30_out, and_31_out, and_33_out, and_34_out, and_35_out, and_36_out, and_37_out, and_38_out,
       and_39_out, D0, D1, D2, D3, D4, D5, D6, D7, decoder_1_out13, or_6_out, or_8_out, r, T0, T2, T3, T4,
       T5, T6, T7, T8, T9, T10, T11, T12, T14, T15, X1, X2, X3, X4, Z_AC;

  Decoder #(.select(4), .enable("false")) decoder_1 (
    .out0(T0), .out1(LDA_IR), .out2(T2), .out3(T3), .out4(T4), .out5(T5), .out6(T6), .out7(T7), .out8(T8),
    .out9(T9), .out10(T10), .out11(T11), .out12(T12), .out13(decoder_1_out13), .out14(T14), .out15(T15),
    .sel(PC_inp));
  Decoder #(.select(3), .enable("false")) decoder_2 (
    .out0(D0), .out1(D1), .out2(D2), .out3(D3), .out4(D4), .out5(D5), .out6(D6), .out7(D7), .sel(IR_input));
  and and_1 (and_1_out, D5, T4);
  and and_2 (X2, D5, T7);
  and and_3 (and_3_out, D3, T4);
  and and_4 (and_4_out, D5, T5);
  and and_5 (and_5_out, D7, T3);
  and and_6 (r, D7, T3);
  and and_7 (and_7_out, D0, T4);
  and and_8 (and_8_out, D1, T4);
  and and_9 (and_9_out, D2, T4);
  or or_1 (X4, and_3_out, and_4_out, and_5_out);
  and and_10 (X1, D4, T4);
  and and_11 (and_11_out, D5, T6);
  and and_12 (and_12_out, D2, T5);
  and and_13 (and_13_out, D7, T3);
  and and_14 (and_14_out, D5, T7);
  and and_15 (and_15_out, D5, T4);
  and and_16 (and_16_out, D0, T4);
  and and_17 (and_17_out, D1, T4);
  and and_18 (and_18_out, D2, T4);
  or or_2 (load, LDA_IR, and_1_out, and_7_out, and_8_out, and_9_out);
  or or_3 (X3, and_11_out, and_12_out);
  or or_4 (LDA_DR, and_13_out, and_14_out, and_15_out, and_16_out, and_17_out, and_18_out);
  and and_19 (and_19_out, D0, T5);
  and and_20 (and_20_out, D1, T5);
  and and_21 (and_21_out, D2, T5);
  and and_22 (and_22_out, D5, T6);
  and and_23 (and_23_out, D5, T8);
  and and_24 (and_24_out, D7, T4);
  and and_25 (and_25_out, D2, T5);
  and and_26 (and_26_out, D5, T6);
  or or_5 (LDA_AR, T0, T2);
  and and_27 (LD_TR, D5, T5);
  or or_6 (or_6_out, AC_inp[0], AC_inp[1], AC_inp[2], AC_inp[3], AC_inp[4], AC_inp[5], AC_inp[6], AC_inp[7], AC_inp[8], AC_inp[9], AC_inp[10], AC_inp[11], AC_inp[12], AC_inp[13], AC_inp[14], AC_inp[15]);
  or or_7 (LDA_AC, and_19_out, and_20_out, and_21_out, and_22_out, and_23_out, and_24_out);
  and and_28 (and_28_out, D5, T8);
  or or_8 (or_8_out, and_25_out, and_26_out);
  not not_1 (Z_AC, or_6_out);
  and and_29 (and_29_out, D1, T5);
  and and_30 (and_30_out, D0, T5);
  and and_31 (and_31_out, D7, T4);
  and and_32 (LDA_PC, D4, T4);
  and and_33 (and_33_out, r, B2, Z_AC);
  Priority_Encoder priority_encoder_1 (
    .in0(1'b0), .in1(and_29_out), .in2(and_28_out), .in3(or_8_out), .in4(and_30_out), .in5(1'b0), .in6(1'b0),
    .in7(and_31_out), .out(ALU));  // open: en_in, gs, en_out
  and and_34 (and_34_out, D0, T5);
  and and_35 (and_35_out, D2, T5);
  and and_36 (and_36_out, D3, T4);
  and and_37 (and_37_out, D4, T4);
  and and_38 (and_38_out, D5, T8);
  and and_39 (and_39_out, D7, T4);
  or or_9 (INC_PC, and_33_out, LDA_IR);
  and and_40 (str, D3, T4);
  or or_10 (clear_sc, and_34_out, and_35_out, and_36_out, and_37_out, and_38_out, and_39_out);
  Priority_Encoder priority_encoder_2 (
    .in0(load), .in1(X1), .in2(X2), .in3(X3), .in4(X4), .in5(T0), .in6(T2), .in7(1'b0), .out(bus));  // open: en_in, gs, en_out

  // Other names for the same wires on the sheet: T1 = LDA_IR; X0 = load
endmodule
